# Fritzing sketch Schematic2 (saved by Fritzing 0.9.3b)
breadboards: 1

parts:
  AMPOP_ELECTROLAB = OP27 - Low Noise, Precision Op Amp [part_number=OP27]
  AMPOP_741 = OP27 - Low Noise, Precision Op Amp [part_number=OP27]
  R1 = Resistor [tolerance=±5% resistance=10k package=THT]
  R1_2 = Resistor [tolerance=±5% resistance=10k package=THT]
  R2 = Resistor [tolerance=±5% resistance=1k package=THT]

nets:
  SONDA pH: AMPOP_ELECTROLAB.+IN
  GND: AMPOP_ELECTROLAB.-V, AMPOP_741.-V
  N1: AMPOP_ELECTROLAB.OUT, R1.Pin_0
  N2: AMPOP_741.-IN, R1_2.Pin_1, R2.Pin_0
  ESP32: AMPOP_741.OUT, R2.Pin_1
  N3: R1.Pin_1, R1_2.Pin_0

notes:
  S
  D
  com
  ElectroLab Sensor pH
  Maquina ElectroLab
